# Fritzing sketch temperature (saved by Fritzing 0.9.2b)
breadboards: 1

parts:
  Raspberry_Pi1 = Raspberry Pi B rev2
  J1_ADAFRUIT_MCP9808 = female pin header, 8 pins [form="♀ (female)"]
  J2_RELAY_MODULE = female pin header, 4 pins [form="♀ (female)"]

nets:
  N1: Raspberry_Pi1.3V3, J1_ADAFRUIT_MCP9808.pin2
  N2: Raspberry_Pi1.5V, J2_RELAY_MODULE.pin4
  N3: Raspberry_Pi1.GPIO_2, J1_ADAFRUIT_MCP9808.pin4
  N4: Raspberry_Pi1.GPIO_3, J1_ADAFRUIT_MCP9808.pin3
  N5: Raspberry_Pi1.GND, J1_ADAFRUIT_MCP9808.pin1, J2_RELAY_MODULE.pin1
  N6: Raspberry_Pi1.GPIO_23, J2_RELAY_MODULE.pin2
  N7: Raspberry_Pi1.GPIO_24, J2_RELAY_MODULE.pin3
